// Logisim project processor.circ as structural Verilog: 11 circuits, main circuit main
module main (
);

  wire CLK, IO_OP, or_1_out, RD_MEM, RD_WR_PORT, RST, WR_MEM;
  wire [7:0] DATA_ADDR, DATA_IN, DATA_MEM_ADDR, DATA_OUT, INST_ADDR, INST_IN, PORT_ADDR, ram_1_data;

  Button u_RST (.out(RST));
  Clock u_CLK (.out(CLK));
  ROM program_memory (.addr(INST_ADDR), .data(INST_IN));
  Demultiplexer #(.disabled("Z"), .enable("true"), .width(8)) demultiplexer_1 (
    .out0(DATA_MEM_ADDR), .out1(PORT_ADDR), .in(DATA_ADDR), .sel(IO_OP), .en(or_1_out));
  or or_1 (or_1_out, RD_MEM, WR_MEM, IO_OP);
  RAM #(.asyncread("true"), .databus("bidir")) ram_1 (
    .addr(DATA_MEM_ADDR), .we(WR_MEM), .oe(RD_MEM), .clk(CLK), .data(ram_1_data));
  cpu cpu_1 (
    .CLK(CLK), .RST(RST), .INST_IN(INST_IN), .DATA_IN(DATA_IN), .INST_ADDR(INST_ADDR), .DATA_OUT(DATA_OUT),
    .DATA_ADDR(DATA_ADDR), .RD_MEM(RD_MEM), .WR_MEM(WR_MEM), .RD_WR_PORT(RD_WR_PORT), .IO_OP(IO_OP));
  gpio_controller gpio_controller_1 (
    .DATA_ADDR(DATA_ADDR), .RD_WR(RD_WR_PORT), .CLK(CLK), .RST(RST), .EN(IO_OP), .DATA_IN(DATA_OUT),
    .DATA_OUT(DATA_IN));
  assign DATA_IN = RD_MEM ? ram_1_data : 8'bz;  // Controlled_Buffer controlled_buffer_1
  assign ram_1_data = WR_MEM ? DATA_OUT : 8'bz;  // Controlled_Buffer controlled_buffer_2

  // Notes on the sheet:
  //   contents of program_memory (hex, n*v repeats v):
  //   50 c5 ad c8 aa 32 f8 a4 c4 aa 42 ae cc a0 c4 aa d0 32 c4 ae cc a0
  //   CRISC-1 8-bit CPU Microcontroller
endmodule

module alu (
  input  [7:0] OP_0,
  input  [7:0] OP_1,
  input  [2:0] OP_SEL,
  input  UNARY_OP,
  input  BINARY_OP,
  output [7:0] RES,
  output ZF
);

  wire [7:0] adder_1_out, adder_2_out, and_1_out, demultiplexer_1_out1, demultiplexer_1_out2,
       demultiplexer_1_out3, demultiplexer_1_out4, demultiplexer_1_out5, demultiplexer_1_out6,
       demultiplexer_1_out7, demultiplexer_2_out1, demultiplexer_2_out2, demultiplexer_2_out3,
       demultiplexer_2_out4, demultiplexer_2_out5, demultiplexer_2_out6, demultiplexer_2_out7,
       demultiplexer_3_out4, demultiplexer_3_out5, demultiplexer_3_out6, demultiplexer_3_out7,
       multiplier_1_out, negator_1_out, not_1_out, or_1_out, subtractor_1_out, subtractor_2_out,
       subtractor_3_out, xor_1_out;

  Demultiplexer #(.enable("true"), .select(3), .width(8)) demultiplexer_1 (
    .out1(demultiplexer_1_out1), .out2(demultiplexer_1_out2), .out3(demultiplexer_1_out3),
    .out4(demultiplexer_1_out4), .out5(demultiplexer_1_out5), .out6(demultiplexer_1_out6),
    .out7(demultiplexer_1_out7), .in(OP_0), .sel(OP_SEL), .en(BINARY_OP));  // open: out0
  Demultiplexer #(.enable("true"), .select(3), .width(8)) demultiplexer_2 (
    .out1(demultiplexer_2_out1), .out2(demultiplexer_2_out2), .out3(demultiplexer_2_out3),
    .out4(demultiplexer_2_out4), .out5(demultiplexer_2_out5), .out6(demultiplexer_2_out6),
    .out7(demultiplexer_2_out7), .in(OP_1), .sel(OP_SEL), .en(BINARY_OP));  // open: out0
  Adder adder_1 (.a(demultiplexer_1_out1), .b(demultiplexer_2_out1), .out(adder_1_out));  // open: cin, cout
  Subtractor subtractor_1 (
    .a(demultiplexer_1_out2), .b(demultiplexer_2_out2), .out(subtractor_1_out));  // open: bin, bout
  assign and_1_out = demultiplexer_1_out3 & demultiplexer_2_out3;  // AND_Gate and_1, 8 bits wide
  assign or_1_out = demultiplexer_1_out4 | demultiplexer_2_out4;  // OR_Gate or_1, 8 bits wide
  assign xor_1_out = demultiplexer_1_out5 ^ demultiplexer_2_out5;  // XOR_Gate xor_1, 8 bits wide
  Multiplier multiplier_1 (
    .a(demultiplexer_1_out6), .b(demultiplexer_2_out6), .out(multiplier_1_out));  // open: cin, cout
  Subtractor subtractor_2 (
    .a(demultiplexer_1_out7), .b(demultiplexer_2_out7), .out(subtractor_2_out));  // open: bin, bout
  Demultiplexer #(.enable("true"), .select(3), .width(8)) demultiplexer_3 (
    .out4(demultiplexer_3_out4), .out5(demultiplexer_3_out5), .out6(demultiplexer_3_out6),
    .out7(demultiplexer_3_out7), .in(OP_0), .sel(OP_SEL), .en(UNARY_OP));  // open: out0, out1, out2, out3
  assign not_1_out = ~demultiplexer_3_out4;  // NOT_Gate not_1, 8 bits wide
  Negator negator_1 (.in(demultiplexer_3_out5), .out(negator_1_out));
  Adder adder_2 (.a(demultiplexer_3_out6), .b(8'h1), .out(adder_2_out));  // open: cin, cout
  Subtractor subtractor_3 (.a(demultiplexer_3_out7), .b(8'h1), .out(subtractor_3_out));  // open: bin, bout
  Multiplexer #(.disabled("Z"), .enable("true"), .select(3), .width(8)) multiplexer_1 (
    .in1(adder_1_out), .in2(subtractor_1_out), .in3(and_1_out), .in4(or_1_out), .in5(xor_1_out),
    .in6(multiplier_1_out), .in7(subtractor_2_out), .out(RES), .sel(OP_SEL), .en(BINARY_OP));  // open: in0
  Multiplexer #(.disabled("Z"), .enable("true"), .select(3), .width(8)) multiplexer_2 (
    .in4(not_1_out), .in5(negator_1_out), .in6(adder_2_out), .in7(subtractor_3_out), .out(RES), .sel(OP_SEL),
    .en(UNARY_OP));  // open: in0, in1, in2, in3
  Comparator comparator_1 (.a(RES), .b({8{1'b0}}), .eq(ZF));  // open: gt, lt

  // Notes on the sheet:
  //   CRISC-1 8-bit Arithmetic-Logic Unit
endmodule

module register_file (
  input  [7:0] DATA_IN,
  input  LOAD,
  input  [1:0] LD_SEL,
  input  CLK,
  input  RST,
  input  [1:0] SRC_SEL,
  input  [1:0] DST_SEL,
  output [7:0] DST,
  output [7:0] SRC
);

  wire decoder_1_out0, decoder_1_out1, decoder_1_out2, decoder_1_out3;
  wire [7:0] register_1_q, register_2_q, register_3_q, register_4_q;

  Decoder #(.select(2)) decoder_1 (
    .out0(decoder_1_out0), .out1(decoder_1_out1), .out2(decoder_1_out2), .out3(decoder_1_out3), .sel(LD_SEL),
    .en(LOAD));
  Register register_1 (.D(DATA_IN), .en(decoder_1_out0), .clk(CLK), .Q(register_1_q), .clr(RST));
  Register register_2 (.D(DATA_IN), .en(decoder_1_out1), .clk(CLK), .Q(register_2_q), .clr(RST));
  Register register_3 (.D(DATA_IN), .en(decoder_1_out2), .clk(CLK), .Q(register_3_q), .clr(RST));
  Register register_4 (.D(DATA_IN), .en(decoder_1_out3), .clk(CLK), .Q(register_4_q), .clr(RST));
  Multiplexer #(.select(2), .width(8)) multiplexer_1 (
    .in0(register_1_q), .in1(register_2_q), .in2(register_3_q), .in3(register_4_q), .out(DST), .sel(DST_SEL));
  Multiplexer #(.select(2), .width(8)) multiplexer_2 (
    .in0(register_1_q), .in1(register_2_q), .in2(register_3_q), .in3(register_4_q), .out(SRC), .sel(SRC_SEL));

  // Notes on the sheet:
  //   CRISC-1 8-bit Register File
  //   DST
  //   SRC
endmodule

module instruction_decoder (
  input  [7:0] INSTR,
  output [1:0] SRC,
  output [2:0] ALU_OP_SEL,
  output LD_ST,
  output COND_BR,
  output IN_OUT,
  output [1:0] DST,
  output [3:0] IMM,
  output BI_ALU_OP,
  output IMM_OP,
  output MEM_OP,
  output UN_ALU_OP,
  output BR_OP,
  output IO_OP,
  output HALT,
  output WB
);

  wire and_1_out, and_2_out, and_3_out, and_4_out, and_5_out, and_6_out, and_7_out, and_8_out, and_9_out,
       and_10_out, and_11_out, nor_1_out, not_1_out, not_2_out, not_3_out, not_4_out, not_5_out, not_6_out,
       not_7_out, not_8_out, not_9_out, not_10_out, or_1_out, priority_encoder_1_gs;
  wire [1:0] multiplexer_2_out;
  wire [2:0] priority_encoder_1_out;

  not not_1 (not_1_out, INSTR[6]);
  not not_2 (not_2_out, INSTR[5]);
  not not_3 (not_3_out, INSTR[6]);
  not not_4 (not_4_out, INSTR[6]);
  not not_5 (not_5_out, INSTR[4]);
  not not_6 (not_6_out, INSTR[3]);
  not not_7 (not_7_out, INSTR[6]);
  not not_8 (not_8_out, INSTR[4]);
  not not_9 (not_9_out, INSTR[7]);
  and and_1 (and_1_out, INSTR[7], INSTR[6]);
  and and_2 (and_2_out, INSTR[7], not_1_out, not_2_out);
  and and_3 (and_3_out, INSTR[7], not_3_out, INSTR[5], INSTR[4]);
  and and_4 (and_4_out, INSTR[7], not_4_out, INSTR[5], not_5_out, not_6_out);
  and and_5 (and_5_out, INSTR[7], not_7_out, INSTR[5], not_8_out, INSTR[3]);
  nor nor_1 (nor_1_out, INSTR[7], INSTR[6], INSTR[5], INSTR[4], INSTR[3], INSTR[2], INSTR[1], INSTR[0]);
  Multiplexer #(.width(3)) multiplexer_1 (.in0(INSTR[4:2]), .in1(INSTR[6:4]), .out(ALU_OP_SEL), .sel(BI_ALU_OP));
  Decoder #(.select(3)) decoder_1 (
    .out0(BI_ALU_OP), .out1(IMM_OP), .out2(MEM_OP), .out3(UN_ALU_OP), .out4(BR_OP), .out5(IO_OP),
    .out6(HALT), .sel(priority_encoder_1_out), .en(priority_encoder_1_gs));  // open: out7
  Priority_Encoder priority_encoder_1 (
    .in0(not_9_out), .in1(and_1_out), .in2(and_2_out), .in3(and_3_out), .in4(and_4_out), .in5(and_5_out),
    .in6(nor_1_out), .out(priority_encoder_1_out), .gs(priority_encoder_1_gs));  // open: in7, en_in, en_out
  and and_6 (and_6_out, IO_OP, INSTR[2]);
  and and_7 (and_7_out, ALU_OP_SEL[0], ALU_OP_SEL[1], ALU_OP_SEL[2], BI_ALU_OP);
  and and_8 (and_8_out, MEM_OP, INSTR[4]);
  nor nor_2 (WB, BR_OP, HALT, and_6_out, and_7_out, and_8_out);
  Multiplexer #(.disabled("Z"), .width(2)) multiplexer_2 (
    .in0(INSTR[3:2]), .in1(INSTR[1:0]), .out(multiplexer_2_out), .sel(or_1_out));
  or or_1 (or_1_out, BR_OP, and_9_out);
  and and_9 (and_9_out, IO_OP, INSTR[2]);
  Multiplexer #(.disabled("Z"), .width(2)) multiplexer_3 (.in0(INSTR[1:0]), .in1(2'b00), .out(DST), .sel(and_10_out));
  and and_10 (and_10_out, IO_OP, INSTR[2]);
  Multiplexer #(.disabled("Z"), .width(2)) multiplexer_4 (
    .in0(multiplexer_2_out), .in1(2'b00), .out(SRC), .sel(and_11_out));
  and and_11 (and_11_out, IO_OP, not_10_out);
  not not_10 (not_10_out, INSTR[2]);

  assign COND_BR = INSTR[2];
  assign IMM = INSTR[5:2];
  assign IN_OUT = INSTR[2];
  assign LD_ST = INSTR[4];
  // also tied to VCC on the sheet: priority_encoder_1_gs

  // Other names for the same wires on the sheet: I6 = INSTR[6]; I0 = INSTR[0]; I1 = INSTR[1]; I2 = INSTR[2];
  //   I3 = INSTR[3]; I4 = INSTR[4]; I5 = INSTR[5]; I7 = INSTR[7]

  // Notes on the sheet:
  //   CRISC-1 8-bit Instruction Decoder
endmodule

module program_counter (
  input  [7:0] VAL,
  input  LOAD,
  input  EN,
  input  CLK,
  input  RST,
  output [7:0] PC
);

  wire not_1_out;
  wire [7:0] adder_1_out, multiplexer_1_out;

  Adder adder_1 (.a(PC), .b({8{1'b0}}), .out(adder_1_out), .cin(EN));  // open: cout
  Multiplexer #(.width(8)) multiplexer_1 (.in0(adder_1_out), .in1(VAL), .out(multiplexer_1_out), .sel(LOAD));
  Register register_1 (.D(multiplexer_1_out), .en(EN), .clk(not_1_out), .Q(PC), .clr(RST));
  not not_1 (not_1_out, CLK);

  // Notes on the sheet:
  //   CRISC-1 8-bit Program Counter
endmodule

module cpu (
  input  CLK,
  input  RST,
  input  [7:0] INST_IN,
  input  [7:0] DATA_IN,
  output [7:0] INST_ADDR,
  output [7:0] DATA_OUT,
  output [7:0] DATA_ADDR,
  output RD_MEM,
  output WR_MEM,
  output RD_WR_PORT,
  output IO_OP
);

  wire BI_ALU_OP, BR_OP, COND_BR, EN, HALT, IMM_OP, LD_ST, MEM_OP, not_1_out, not_2_out, or_1_out, or_2_out,
       or_3_out, or_4_out, RD_PORT, UN_ALU_OP, WB, WR_PORT, ZF;
  wire [1:0] DST_SEL, SRC_SEL;
  wire [2:0] ALU_OP_SEL;
  wire [3:0] IMM;
  wire [7:0] ALU_RES, DST, multiplexer_1_out, multiplexer_2_out, SRC;

  not not_1 (not_1_out, LD_ST);
  not not_2 (not_2_out, RD_WR_PORT);
  Multiplexer #(.width(8)) multiplexer_1 (.in0(ALU_RES), .in1({4'b0000, IMM}), .out(multiplexer_1_out), .sel(IMM_OP));
  not not_3 (EN, HALT);
  and and_1 (RD_MEM, MEM_OP, not_1_out);
  and and_2 (WR_MEM, MEM_OP, LD_ST);
  and and_3 (RD_PORT, IO_OP, not_2_out);
  and and_4 (WR_PORT, IO_OP, RD_WR_PORT);
  or or_1 (or_1_out, RD_MEM, RD_PORT);
  Multiplexer #(.width(8)) multiplexer_2 (
    .in0(multiplexer_1_out), .in1(DATA_IN), .out(multiplexer_2_out), .sel(or_1_out));
  register_file register_file_1 (
    .DATA_IN(multiplexer_2_out), .LOAD(WB), .LD_SEL(DST_SEL), .CLK(CLK), .RST(RST), .SRC_SEL(SRC_SEL),
    .DST_SEL(DST_SEL), .DST(DST), .SRC(SRC));
  Multiplexer #(.disabled("Z"), .enable("true"), .width(8)) multiplexer_3 (
    .in0(SRC), .in1(DST), .out(DATA_ADDR), .sel(or_2_out), .en(or_4_out));
  or or_2 (or_2_out, WR_MEM, WR_PORT);
  control_unit control_unit_1 (
    .PC_VAL(SRC), .ZF(ZF), .CLK(CLK), .RST(RST), .EN(EN), .INST_IN(INST_IN), .BI_ALU_OP(BI_ALU_OP),
    .IMM_OP(IMM_OP), .MEM_OP(MEM_OP), .HALT(HALT), .LD_ST(LD_ST), .ALU_OP_SEL(ALU_OP_SEL), .SRC_SEL(SRC_SEL),
    .DST_SEL(DST_SEL), .IMM(IMM), .INST_ADDR(INST_ADDR), .COND_BR(COND_BR), .WB(WB), .UN_ALU_OP(UN_ALU_OP),
    .BR_OP(BR_OP), .IO_OP(IO_OP), .IN_OUT(RD_WR_PORT));
  assign DATA_OUT = or_3_out ? SRC : 8'bz;  // Controlled_Buffer controlled_buffer_1
  or or_3 (or_3_out, WR_PORT, WR_MEM);
  or or_4 (or_4_out, MEM_OP, IO_OP);
  alu alu_1 (
    .OP_0(DST), .OP_1(SRC), .OP_SEL(ALU_OP_SEL), .UNARY_OP(UN_ALU_OP), .BINARY_OP(BI_ALU_OP), .RES(ALU_RES),
    .ZF(ZF));

  // Other names for the same wires on the sheet: IN_OUT = RD_WR_PORT

  // Notes on the sheet:
  //   CRISC-1 8-bit CPU
endmodule

module control_unit (
  input  [7:0] PC_VAL,
  input  ZF,
  input  CLK,
  input  RST,
  input  EN,
  input  [7:0] INST_IN,
  output BI_ALU_OP,
  output IMM_OP,
  output MEM_OP,
  output HALT,
  output LD_ST,
  output [2:0] ALU_OP_SEL,
  output [1:0] SRC_SEL,
  output [1:0] DST_SEL,
  output [3:0] IMM,
  output [7:0] INST_ADDR,
  output COND_BR,
  output WB,
  output UN_ALU_OP,
  output BR_OP,
  output IO_OP,
  output IN_OUT
);

  wire FLAG, LOAD_PC, not_1_out, or_1_out;
  wire [7:0] instruction_register_q;

  Register instruction_register (.D(INST_IN), .clk(CLK), .Q(instruction_register_q), .clr(RST));  // open: en
  program_counter program_counter_1 (.VAL(PC_VAL), .LOAD(LOAD_PC), .EN(EN), .CLK(CLK), .RST(RST), .PC(INST_ADDR));
  or or_1 (or_1_out, FLAG, not_1_out);
  not not_1 (not_1_out, COND_BR);
  and and_1 (LOAD_PC, BR_OP, or_1_out);
  instruction_decoder instruction_decoder_1 (
    .INSTR(instruction_register_q), .SRC(SRC_SEL), .ALU_OP_SEL(ALU_OP_SEL), .LD_ST(LD_ST), .COND_BR(COND_BR),
    .IN_OUT(IN_OUT), .DST(DST_SEL), .IMM(IMM), .BI_ALU_OP(BI_ALU_OP), .IMM_OP(IMM_OP), .MEM_OP(MEM_OP),
    .UN_ALU_OP(UN_ALU_OP), .BR_OP(BR_OP), .IO_OP(IO_OP), .HALT(HALT), .WB(WB));
  D_Flip_Flop flag_register (.D(ZF), .clk(CLK), .Q(FLAG), .reset(RST));  // open: Qn, preset

  // Other names for the same wires on the sheet: INST[7:0] = INST_IN; PC[7:0] = INST_ADDR

  // Notes on the sheet:
  //   CRISC-1 8-bit Control Unit
  //   Control Signals
endmodule

module gpio_interface (
  input  [7:0] PORT_IN,
  input  [7:0] LOAD_DIN,
  input  CLK,
  input  RST,
  input  WE,
  input  [1:0] SEL,
  output [7:0] PORT_OUT,
  output [7:0] DATA_DIR,
  output [7:0] DATA_OUT,
  output [7:0] DATA_IN
);

  wire WE_DIR, WE_DOUT;

  Register register_1 (.D(PORT_IN), .en(WE_DIR), .clk(CLK), .Q(DATA_DIR), .clr(RST));
  Register register_2 (.D(PORT_IN), .en(WE_DOUT), .clk(CLK), .Q(DATA_OUT), .clr(RST));
  Register register_3 (.D(LOAD_DIN), .en(WE), .clk(CLK), .Q(DATA_IN), .clr(RST));
  Decoder decoder_1 (.out0(WE_DIR), .out1(WE_DOUT), .sel(SEL[0]), .en(WE));
  Multiplexer #(.select(2), .width(8)) multiplexer_1 (
    .in0(DATA_DIR), .in1(DATA_OUT), .in2(DATA_IN), .out(PORT_OUT), .sel(SEL));  // open: in3

  // Notes on the sheet:
  //   CRISC-1 I/O Interface Registers
endmodule

module gpio_port_a (
  input  [7:0] PORT_IN,
  input  CLK,
  input  RST,
  input  RD_WR,
  input  [1:0] SEL,
  output [7:0] PORT_OUT
);

  wire not_1_out, not_2_out, not_3_out, not_4_out, not_5_out, not_6_out, not_7_out, not_8_out, P0, P1, P2,
       P3, P4, P5, P6, P7;
  wire [7:0] DATA_DIR, DATA_IN, DATA_OUT, LOAD_DIN;

  DipSwitch #(.number(2)) dipswitch_1 (.sw1(P1));  // open: sw2
  LED led_1 (.in(P0));
  gpio_interface gpio_interface_1 (
    .PORT_IN(PORT_IN), .LOAD_DIN(LOAD_DIN), .CLK(CLK), .RST(RST), .WE(RD_WR), .SEL(SEL), .PORT_OUT(PORT_OUT),
    .DATA_DIR(DATA_DIR), .DATA_OUT(DATA_OUT), .DATA_IN(DATA_IN));
  assign P0 = DATA_DIR[0] ? DATA_OUT[0] : 1'bz;  // Controlled_Buffer controlled_buffer_1
  not not_1 (not_1_out, DATA_DIR[0]);
  assign LOAD_DIN[0] = not_1_out ? P0 : 1'bz;  // Controlled_Buffer controlled_buffer_2
  assign P1 = DATA_DIR[1] ? DATA_OUT[1] : 1'bz;  // Controlled_Buffer controlled_buffer_3
  not not_2 (not_2_out, DATA_DIR[1]);
  assign LOAD_DIN[1] = not_2_out ? P1 : 1'bz;  // Controlled_Buffer controlled_buffer_4
  assign P2 = DATA_DIR[2] ? DATA_OUT[2] : 1'bz;  // Controlled_Buffer controlled_buffer_5
  not not_3 (not_3_out, DATA_DIR[2]);
  assign LOAD_DIN[2] = not_3_out ? P2 : 1'bz;  // Controlled_Buffer controlled_buffer_6
  assign P3 = DATA_DIR[3] ? DATA_OUT[3] : 1'bz;  // Controlled_Buffer controlled_buffer_7
  not not_4 (not_4_out, DATA_DIR[3]);
  assign LOAD_DIN[3] = not_4_out ? P3 : 1'bz;  // Controlled_Buffer controlled_buffer_8
  Pull_Resistor pull_resistor_1 (.node(P0));
  Pull_Resistor pull_resistor_2 (.node(P1));
  Pull_Resistor pull_resistor_3 (.node(P2));
  Pull_Resistor pull_resistor_4 (.node(P3));
  assign P4 = DATA_DIR[4] ? DATA_OUT[4] : 1'bz;  // Controlled_Buffer controlled_buffer_9
  not not_5 (not_5_out, DATA_DIR[4]);
  assign LOAD_DIN[4] = not_5_out ? P4 : 1'bz;  // Controlled_Buffer controlled_buffer_10
  assign P5 = DATA_DIR[5] ? DATA_OUT[5] : 1'bz;  // Controlled_Buffer controlled_buffer_11
  not not_6 (not_6_out, DATA_DIR[5]);
  assign LOAD_DIN[5] = not_6_out ? P5 : 1'bz;  // Controlled_Buffer controlled_buffer_12
  assign P6 = DATA_DIR[6] ? DATA_OUT[6] : 1'bz;  // Controlled_Buffer controlled_buffer_13
  not not_7 (not_7_out, DATA_DIR[6]);
  assign LOAD_DIN[6] = not_7_out ? P6 : 1'bz;  // Controlled_Buffer controlled_buffer_14
  assign P7 = DATA_DIR[7] ? DATA_OUT[7] : 1'bz;  // Controlled_Buffer controlled_buffer_15
  not not_8 (not_8_out, DATA_DIR[7]);
  assign LOAD_DIN[7] = not_8_out ? P7 : 1'bz;  // Controlled_Buffer controlled_buffer_16
  Pull_Resistor pull_resistor_5 (.node(P4));
  Pull_Resistor pull_resistor_6 (.node(P5));
  Pull_Resistor pull_resistor_7 (.node(P6));
  Pull_Resistor pull_resistor_8 (.node(P7));

  // Other names for the same wires on the sheet: P0_DATA_DIR = DATA_DIR[0]; P1_DATA_DIR = DATA_DIR[1];
  //   P2_DATA_DIR = DATA_DIR[2]; P3_DATA_DIR = DATA_DIR[3]; P4_DATA_DIR = DATA_DIR[4]; P5_DATA_DIR = DATA_DIR[5];
  //   P6_DATA_DIR = DATA_DIR[6]; P7_DATA_DIR = DATA_DIR[7]; P0_DATA_OUT = DATA_OUT[0]; P1_DATA_OUT = DATA_OUT[1];
  //   P2_DATA_OUT = DATA_OUT[2]; P3_DATA_OUT = DATA_OUT[3]; P4_DATA_OUT = DATA_OUT[4]; P5_DATA_OUT = DATA_OUT[5];
  //   P6_DATA_OUT = DATA_OUT[6]; P7_DATA_OUT = DATA_OUT[7]; P0_DATA_IN = LOAD_DIN[0]; P1_DATA_IN = LOAD_DIN[1];
  //   P2_DATA_IN = LOAD_DIN[2]; P3_DATA_IN = LOAD_DIN[3]; P4_DATA_IN = LOAD_DIN[4]; P5_DATA_IN = LOAD_DIN[5];
  //   P6_DATA_IN = LOAD_DIN[6]; P7_DATA_IN = LOAD_DIN[7]

  // Notes on the sheet:
  //   CRISC-1 I/O PORT A
endmodule

module gpio_port_b (
  input  [7:0] PORT_IN,
  input  CLK,
  input  RST,
  input  RD_WR,
  input  [1:0] SEL,
  output [7:0] PORT_OUT,
  output [7:0] DATA_DIR,
  output [7:0] DATA_OUT,
  output [7:0] DATA_IN
);

  wire not_1_out, not_2_out, not_3_out, not_4_out, not_5_out, not_6_out, not_7_out, not_8_out, P0, P1, P2,
       P3, P4, P5, P6, P7;
  wire [7:0] LOAD_DIN;

  gpio_interface gpio_interface_1 (
    .PORT_IN(PORT_IN), .LOAD_DIN(LOAD_DIN), .CLK(CLK), .RST(RST), .WE(RD_WR), .SEL(SEL), .PORT_OUT(PORT_OUT),
    .DATA_DIR(DATA_DIR), .DATA_OUT(DATA_OUT), .DATA_IN(DATA_IN));
  assign P0 = DATA_DIR[0] ? DATA_OUT[0] : 1'bz;  // Controlled_Buffer controlled_buffer_1
  not not_1 (not_1_out, DATA_DIR[0]);
  assign LOAD_DIN[0] = not_1_out ? P0 : 1'bz;  // Controlled_Buffer controlled_buffer_2
  assign P1 = DATA_DIR[1] ? DATA_OUT[1] : 1'bz;  // Controlled_Buffer controlled_buffer_3
  not not_2 (not_2_out, DATA_DIR[1]);
  assign LOAD_DIN[1] = not_2_out ? P1 : 1'bz;  // Controlled_Buffer controlled_buffer_4
  assign P2 = DATA_DIR[2] ? DATA_OUT[2] : 1'bz;  // Controlled_Buffer controlled_buffer_5
  not not_3 (not_3_out, DATA_DIR[2]);
  assign LOAD_DIN[2] = not_3_out ? P2 : 1'bz;  // Controlled_Buffer controlled_buffer_6
  assign P3 = DATA_DIR[3] ? DATA_OUT[3] : 1'bz;  // Controlled_Buffer controlled_buffer_7
  not not_4 (not_4_out, DATA_DIR[3]);
  assign LOAD_DIN[3] = not_4_out ? P3 : 1'bz;  // Controlled_Buffer controlled_buffer_8
  Pull_Resistor pull_resistor_1 (.node(P0));
  Pull_Resistor pull_resistor_2 (.node(P1));
  Pull_Resistor pull_resistor_3 (.node(P2));
  Pull_Resistor pull_resistor_4 (.node(P3));
  assign P4 = DATA_DIR[4] ? DATA_OUT[4] : 1'bz;  // Controlled_Buffer controlled_buffer_9
  not not_5 (not_5_out, DATA_DIR[4]);
  assign LOAD_DIN[4] = not_5_out ? P4 : 1'bz;  // Controlled_Buffer controlled_buffer_10
  assign P5 = DATA_DIR[5] ? DATA_OUT[5] : 1'bz;  // Controlled_Buffer controlled_buffer_11
  not not_6 (not_6_out, DATA_DIR[5]);
  assign LOAD_DIN[5] = not_6_out ? P5 : 1'bz;  // Controlled_Buffer controlled_buffer_12
  assign P6 = DATA_DIR[6] ? DATA_OUT[6] : 1'bz;  // Controlled_Buffer controlled_buffer_13
  not not_7 (not_7_out, DATA_DIR[6]);
  assign LOAD_DIN[6] = not_7_out ? P6 : 1'bz;  // Controlled_Buffer controlled_buffer_14
  assign P7 = DATA_DIR[7] ? DATA_OUT[7] : 1'bz;  // Controlled_Buffer controlled_buffer_15
  not not_8 (not_8_out, DATA_DIR[7]);
  assign LOAD_DIN[7] = not_8_out ? P7 : 1'bz;  // Controlled_Buffer controlled_buffer_16
  Pull_Resistor pull_resistor_5 (.node(P4));
  Pull_Resistor pull_resistor_6 (.node(P5));
  Pull_Resistor pull_resistor_7 (.node(P6));
  Pull_Resistor pull_resistor_8 (.node(P7));

  // Other names for the same wires on the sheet: P0_DATA_DIR = DATA_DIR[0]; P1_DATA_DIR = DATA_DIR[1];
  //   P2_DATA_DIR = DATA_DIR[2]; P3_DATA_DIR = DATA_DIR[3]; P4_DATA_DIR = DATA_DIR[4]; P5_DATA_DIR = DATA_DIR[5];
  //   P6_DATA_DIR = DATA_DIR[6]; P7_DATA_DIR = DATA_DIR[7]; P0_DATA_OUT = DATA_OUT[0]; P1_DATA_OUT = DATA_OUT[1];
  //   P2_DATA_OUT = DATA_OUT[2]; P3_DATA_OUT = DATA_OUT[3]; P4_DATA_OUT = DATA_OUT[4]; P5_DATA_OUT = DATA_OUT[5];
  //   P6_DATA_OUT = DATA_OUT[6]; P7_DATA_OUT = DATA_OUT[7]; P0_DATA_IN = LOAD_DIN[0]; P1_DATA_IN = LOAD_DIN[1];
  //   P2_DATA_IN = LOAD_DIN[2]; P3_DATA_IN = LOAD_DIN[3]; P4_DATA_IN = LOAD_DIN[4]; P5_DATA_IN = LOAD_DIN[5];
  //   P6_DATA_IN = LOAD_DIN[6]; P7_DATA_IN = LOAD_DIN[7]

  // Notes on the sheet:
  //   CRISC-1 I/O PORT B
endmodule

module gpio_controller (
  input  [7:0] DATA_ADDR,
  input  RD_WR,
  input  CLK,
  input  RST,
  input  EN,
  input  [7:0] DATA_IN,
  output [7:0] DATA_OUT
);

  wire decoder_1_out0, decoder_1_out1, decoder_1_out2, decoder_1_out3, EN_WR;
  wire [1:0] SEL;

  and and_1 (EN_WR, RD_WR, EN);
  Decoder #(.select(4)) decoder_1 (
    .out0(decoder_1_out0), .out1(decoder_1_out1), .out2(decoder_1_out2), .out3(decoder_1_out3),
    .sel(DATA_ADDR[3:0]), .en(EN));  // open: out4, out5, out6, out7, out8, out9, out10, out11, out12, out13, out14, out15
  Priority_Encoder #(.select(2)) priority_encoder_1 (
    .in0(decoder_1_out0), .in1(decoder_1_out1), .in2(decoder_1_out2), .in3(decoder_1_out3), .out(SEL));  // open: gs, en_out, en_in
  gpio_port_a gpio_port_a_1 (.PORT_IN(DATA_IN), .CLK(CLK), .RST(RST), .RD_WR(EN_WR), .SEL(SEL), .PORT_OUT(DATA_OUT));

  // Notes on the sheet:
  //   CRISC-1 I/O CONTROLLER
endmodule
